# Fritzing sketch layout (saved by Fritzing 0.9.3b)
perfboards: 1

parts:
  Часть1 = Arduino Nano (Rev3.0)
  J1 = double row male pin header, 2 pins [form="♂ (male)"]
  J2 = double row male pin header, 2 pins [form="♂ (male)"]
  C2 = Ceramic Capacitor [capacitance=100nF package="100 mil [THT, multilayer]"]  # not connected
  R2 = Resistor [tolerance=±5% resistance=10k package=THT]
  R3 = Resistor [tolerance=±5% resistance=10k package=THT]
  PN2222A1 = NPN-Transistor [package="TO92 [THT]"]
  J3 = male pin header, 1 pin [form="♂ (male)"]

nets:
  N1: Часть1.GND, J1.pin1, J2.pin1, PN2222A1.E
  N2: Часть1.D2, J2.pin2
  N3: Часть1.D3, R2.Pin_1, R3.Pin_0
  N4: Часть1.VIN, J1.pin2
  N5: Часть1.5V, R3.Pin_1
  N6: R2.Pin_0, PN2222A1.B
  N7: PN2222A1.C, J3.pin1
