# Fritzing sketch sheme (saved by Fritzing 0.9.3b)
stripboards: 1

parts:
  Часть1 = Arduino Nano (Rev3.0)
  Button = Pushbutton [package="[THT]"]
  Power_plug_12VDC = Power plug
  C1 = Ceramic Capacitor [capacitance=0.1mF package="100 mil [THT, multilayer]"]
  Dimmer_control = male pin header, 2 pins [form="♂ (male)" part_number="GND, 10VDC"]
  PN2222A = NPN-Transistor [package="TO92 [THT]"]
  R1 = Resistor [tolerance=±5% resistance=10k package=THT]
  R2 = Resistor [tolerance=±5% resistance=10k package=THT]

nets:
  GND: Часть1.GND, Button.Pin_1, Button.Pin_2, Power_plug_12VDC.GND, C1.1, Dimmer_control.pin2, PN2222A.E
  N1: Часть1.D2, Button.Pin_3, Button.Pin_4, C1.0
  N2: Часть1.D3, R1.Pin_0, R2.Pin_0
  VIN: Часть1.VIN, Power_plug_12VDC.VCC
  N3: Часть1.5V, R1.Pin_1
  N4: Dimmer_control.pin1, PN2222A.C
  N5: PN2222A.B, R2.Pin_1
